// Logisim project serial.circ as structural Verilog: 1 circuit, main circuit main
module main (
);

  wire clock_1_out;
  wire [2:0] shift_register_4_out;
  wire [7:0] ram_1_data, register_1_q, rom_1_data, rom_2_data, shift_register_2_out, shift_register_5_out;
  wire [15:8] shift_register_3_out;

  RAM #(.addrWidth(16), .asyncread("true"), .databus("bidir"), .\type ("nonvolatile")) ram_1 (
    .addr({shift_register_3_out, shift_register_5_out}), .we(rom_1_data[6]), .oe(rom_1_data[5]),
    .clk(clock_1_out), .data(ram_1_data));
  ROM #(.addrWidth(13)) rom_1 (
    .addr({register_1_q, 2'b00, shift_register_4_out[2], shift_register_5_out[0], shift_register_4_out[0]}),
    .data(rom_1_data));
  assign ram_1_data = rom_1_data[6] ? shift_register_2_out : 8'bz;  // Controlled_Buffer controlled_buffer_1
  Clock clock_1 (.out(clock_1_out));
  ROM #(.addrWidth(13)) rom_2 (
    .addr({register_1_q, 2'b00, shift_register_4_out[2], shift_register_5_out[0], shift_register_4_out[0]}),
    .data(rom_2_data));
  Shift_Register shift_register_1 (
    .shift(rom_1_data[4]), .in(1'b0), .clk(clock_1_out), .out(shift_register_4_out[2]), .load(rom_1_data[5]),
    .d0(ram_1_data[7]), .d1(ram_1_data[6]), .d2(ram_1_data[5]), .d3(ram_1_data[4]), .d4(ram_1_data[3]),
    .d5(ram_1_data[2]), .d6(ram_1_data[1]), .d7(ram_1_data[0]));  // open: clr, q0, q1, q2, q3, q4, q5, q6, q7
  Shift_Register shift_register_2 (
    .shift(rom_1_data[0]), .in(rom_1_data[1]), .clk(clock_1_out), .out(shift_register_2_out[0]),
    .q0(shift_register_2_out[7]), .q1(shift_register_2_out[6]), .q2(shift_register_2_out[5]),
    .q3(shift_register_2_out[4]), .q4(shift_register_2_out[3]), .q5(shift_register_2_out[2]),
    .q6(shift_register_2_out[1]));  // open: load, clr, d0, d1, d2, d3, d4, d5, d6, d7, q7
  Shift_Register shift_register_3 (
    .shift(rom_1_data[2]), .in(rom_1_data[3]), .clk(clock_1_out), .out(shift_register_3_out[8]),
    .q0(shift_register_3_out[15]), .q1(shift_register_3_out[14]), .q2(shift_register_3_out[13]),
    .q3(shift_register_3_out[12]), .q4(shift_register_3_out[11]), .q5(shift_register_3_out[10]),
    .q6(shift_register_3_out[9]));  // open: load, clr, d0, d1, d2, d3, d4, d5, d6, d7, q7
  Register register_1 (.D(rom_2_data), .Q(register_1_q), .clk(clock_1_out));  // open: en, clr
  Shift_Register shift_register_4 (
    .shift(rom_1_data[0]), .in(shift_register_2_out[0]), .clk(clock_1_out), .out(shift_register_4_out[0]));  // open: load, clr, d0, q0, d1, q1, d2, q2, d3, q3, d4, q4, d5, q5, d6, q6, d7, q7
  Shift_Register shift_register_5 (
    .shift(rom_1_data[2]), .in(shift_register_3_out[8]), .clk(clock_1_out), .out(shift_register_5_out[0]),
    .q0(shift_register_5_out[7]), .q1(shift_register_5_out[6]), .q2(shift_register_5_out[5]),
    .q3(shift_register_5_out[4]), .q4(shift_register_5_out[3]), .q5(shift_register_5_out[2]),
    .q6(shift_register_5_out[1]));  // open: load, clr, d0, d1, d2, d3, d4, d5, d6, d7, q7

  // Notes on the sheet:
  //   contents of rom_1 (hex, n*v repeats v):
  //   8*4 24*0 8*4 24*0 8*4 24*0 8*4 24*0 8*4 24*0 8*4 24*0 8*4 24*0 8*4 24*0 8*4 24*0 8*4 24*0 8*4 24*0
  //   8*4 24*0 8*4 24*0 8*4 24*0 8*4 24*0 8*4 24*0 8*20 24*0 4*13 4*11 24*0 4*11 4*13 24*0 4*13 4*11 24*0
  //   4*11 4*13 24*0 4*13 4*11 24*0 4*11 4*13 24*0 4*13 4*11 24*0 4*11 4*13 24*0 4*13 4*11 24*0 4*11 4*13
  //   24*0 4*13 4*11 24*0 4*11 4*13 24*0 4*13 4*11 24*0 4*11 4*13 24*0 4*13 4*11 24*0 8*40 24*0 8*c 24*0
  //   8*4 24*0 8*4 24*0 8*4 24*0 8*4 24*0 8*4 24*0 8*4 24*0 8*4 24*0 8*4 24*0 8*4 24*0 8*4 24*0 8*4 24*0
  //   8*4 24*0 8*4 24*0 8*4 24*0 8*4 24*0 21 23 21 23 21 23 21 23 24*0 21 23 21 23 21 23 21 23 24*0 21 23
  //   21 23 21 23 21 23 24*0 21 23 21 23 21 23 21 23 24*0 21 23 21 23 21 23 21 23 24*0 21 23 21 23 21 23
  //   21 23 24*0 21 23 21 23 21 23 21 23 24*0 21 23 21 23 21 23 21 23 24*0 5 d 5 d 5 d 5 d 24*0 5 d 5 d 5
  //   d 5 d 24*0 5 d 5 d 5 d 5 d 24*0 5 d 5 d 5 d 5 d 24*0 5 d 5 d 5 d 5 d 24*0 5 d 5 d 5 d 5 d 24*0 5 d 5
  //   d 5 d 5 d 24*0 5 d 5 d 5 d 5 d 24*0 4*14 4*1c 24*0 4*14 4*1c 24*0 4*14 4*1c 24*0 4*14 4*1c 24*0 4*14
  //   4*1c 24*0 4*14 4*1c 24*0 4*14 4*1c 24*0 4*14 4*1c 24*0 21 23 21 23 21 23 21 23 24*0 21 23 21 23 21
  //   23 21 23 24*0 21 23 21 23 21 23 21 23 24*0 21 23 21 23 21 23 21 23 24*0 21 23 21 23 21 23 21 23 24*0
  //   21 23 21 23 21 23 21 23 24*0 21 23 21 23 21 23 21 23 24*0 21 23 21 23 21 23 21 23 24*0 4*14 4*1c
  //   24*0 4*14 4*1c 24*0 4*14 4*1c 24*0 4*14 4*1c 24*0 4*14 4*1c 24*0 4*14 4*1c 24*0 4*14 4*1c 24*0 4*14
  //   4*1c 24*0 8*4 24*0 8*4 24*0 8*4 24*0 8*4 24*0 8*4 24*0 8*4 24*0 8*4 24*0 8*4
  //   contents of rom_2 (hex, n*v repeats v):
  //   8*1 24*0 8*2 24*0 8*3 24*0 8*4 24*0 8*5 24*0 8*6 24*0 8*7 24*0 8*8 24*0 8*9 24*0 8*a 24*0 8*b 24*0
  //   8*c 24*0 8*d 24*0 8*e 24*0 8*f 24*0 8*10 24*0 8*11 24*0 4*12 4*13 24*0 8*14 24*0 4*14 4*15 24*0 8*16
  //   24*0 4*16 4*17 24*0 8*18 24*0 4*18 4*19 24*0 8*1a 24*0 4*1a 4*1b 24*0 8*1c 24*0 4*1c 4*1d 24*0 8*1e
  //   24*0 4*1e 4*1f 24*0 8*20 24*0 8*20 24*0 8*21 24*0 8*22 24*0 8*23 24*0 8*24 24*0 8*25 24*0 8*26 24*0
  //   8*27 24*0 8*28 24*0 8*29 24*0 8*2a 24*0 8*2b 24*0 8*2c 24*0 8*2d 24*0 8*2e 24*0 8*2f 24*0 8*30 24*0
  //   8*31 24*0 8*32 24*0 8*33 24*0 8*34 24*0 8*35 24*0 8*36 24*0 8*37 24*0 8*38 24*0 8*39 24*0 8*3a 24*0
  //   8*3b 24*0 8*3c 24*0 8*3d 24*0 8*3e 24*0 8*3f 24*0 8*40 24*0 8*41 24*0 8*42 24*0 8*43 24*0 8*44 24*0
  //   8*45 24*0 8*46 24*0 8*47 24*0 8*48 24*0 8*49 24*0 8*4a 24*0 8*4b 24*0 8*4c 24*0 8*4d 24*0 8*4e 24*0
  //   8*4f 24*0 8*50 24*0 8*51 24*0 8*52 24*0 8*53 24*0 8*54 24*0 8*55 24*0 8*56 24*0 8*57 24*0 8*58 24*0
  //   8*59 24*0 8*5a 24*0 8*5b 24*0 8*5c 24*0 8*5d 24*0 8*5e 24*0 8*5f 24*0 8*60 24*0 8*61
  //   T register
  //   X register
  //   A register
endmodule
